// Logisim project processador8bits.circ as structural Verilog: 16 circuits, main circuit main
module main (
  input  OP0,
  input  OP1,
  input  OP2,
  input  B7,
  input  A7,
  input  B6,
  input  A6,
  input  B5,
  input  A5,
  input  B4,
  input  A4,
  input  B3,
  input  A3,
  input  B2,
  input  A2,
  input  B1,
  input  A1,
  input  B0,
  input  A0
);

  wire alu8bits_1_bt, alu8bits_1_c0, alu8bits_1_c1, alu8bits_1_c2, alu8bits_1_c3, alu8bits_1_c4,
       alu8bits_1_c5, alu8bits_1_c6, alu8bits_1_c7, alu8bits_1_cout, alu8bits_1_eq, alu8bits_1_lw,
       decimal_to_hexa_1_s_a, decimal_to_hexa_1_s_b, decimal_to_hexa_1_s_c, decimal_to_hexa_1_s_d,
       decimal_to_hexa_1_s_e, decimal_to_hexa_1_s_f, decimal_to_hexa_1_s_g, decimal_to_hexa_2_s_a,
       decimal_to_hexa_2_s_b, decimal_to_hexa_2_s_c, decimal_to_hexa_2_s_d, decimal_to_hexa_2_s_e,
       decimal_to_hexa_2_s_f, decimal_to_hexa_2_s_g, registrador4bits_1_q0, registrador4bits_1_q1,
       registrador4bits_1_q2, registrador4bits_1_q3, registrador4bits_2_q0, registrador4bits_2_q1,
       registrador4bits_2_q2, registrador4bits_2_q3;

  ALU8bits alu8bits_1 (
    .OP0(OP0), .OP1(OP1), .OP2(OP2), .B7(B7), .A7(A7), .B6(B6), .A6(A6), .B5(B5), .A5(A5), .B4(B4), .A4(A4),
    .B3(B3), .A3(A3), .B2(B2), .A2(A2), .B1(B1), .A1(A1), .B0(B0), .A0(A0), .cout(alu8bits_1_cout),
    .C7(alu8bits_1_c7), .C6(alu8bits_1_c6), .C5(alu8bits_1_c5), .C4(alu8bits_1_c4), .C3(alu8bits_1_c3),
    .C2(alu8bits_1_c2), .C1(alu8bits_1_c1), .C0(alu8bits_1_c0), .EQ(alu8bits_1_eq), .LW(alu8bits_1_lw),
    .BT(alu8bits_1_bt));
  registrador4bits registrador4bits_1 (
    .A3(alu8bits_1_c7), .A2(alu8bits_1_c6), .A1(alu8bits_1_c5), .A0(alu8bits_1_c4),
    .Q3(registrador4bits_1_q3), .Q2(registrador4bits_1_q2), .Q1(registrador4bits_1_q1),
    .Q0(registrador4bits_1_q0));
  registrador4bits registrador4bits_2 (
    .A3(alu8bits_1_c3), .A2(alu8bits_1_c2), .A1(alu8bits_1_c1), .A0(alu8bits_1_c0),
    .Q3(registrador4bits_2_q3), .Q2(registrador4bits_2_q2), .Q1(registrador4bits_2_q1),
    .Q0(registrador4bits_2_q0));
  decimal_to_hexa decimal_to_hexa_1 (
    .A(registrador4bits_1_q3), .B(registrador4bits_1_q2), .C(registrador4bits_1_q1),
    .D(registrador4bits_1_q0), .s_a(decimal_to_hexa_1_s_a), .s_b(decimal_to_hexa_1_s_b),
    .s_c(decimal_to_hexa_1_s_c), .s_d(decimal_to_hexa_1_s_d), .s_e(decimal_to_hexa_1_s_e),
    .s_f(decimal_to_hexa_1_s_f), .s_g(decimal_to_hexa_1_s_g));
  decimal_to_hexa decimal_to_hexa_2 (
    .A(registrador4bits_2_q3), .B(registrador4bits_2_q2), .C(registrador4bits_2_q1),
    .D(registrador4bits_2_q0), .s_a(decimal_to_hexa_2_s_a), .s_b(decimal_to_hexa_2_s_b),
    .s_c(decimal_to_hexa_2_s_c), .s_d(decimal_to_hexa_2_s_d), .s_e(decimal_to_hexa_2_s_e),
    .s_f(decimal_to_hexa_2_s_f), .s_g(decimal_to_hexa_2_s_g));
  LED EQ (.in(alu8bits_1_eq));
  LED LW (.in(alu8bits_1_lw));
  LED BT (.in(alu8bits_1_bt));
  _7_Segment_Display u_7_segment_display_1 (
    .g(decimal_to_hexa_1_s_g), .f(decimal_to_hexa_1_s_f), .a(decimal_to_hexa_1_s_a),
    .b(decimal_to_hexa_1_s_b), .e(decimal_to_hexa_1_s_e), .d(decimal_to_hexa_1_s_d), .c(decimal_to_hexa_1_s_c));  // open: dp
  _7_Segment_Display u_7_segment_display_2 (
    .g(decimal_to_hexa_2_s_g), .f(decimal_to_hexa_2_s_f), .a(decimal_to_hexa_2_s_a),
    .b(decimal_to_hexa_2_s_b), .e(decimal_to_hexa_2_s_e), .d(decimal_to_hexa_2_s_d), .c(decimal_to_hexa_2_s_c));  // open: dp
  // also tied to GND on the sheet: alu8bits_1_cout

  // Notes on the sheet:
  //   0 0 0 -> Soma
  //   1 0 0 - > Sub
  //   0 1 0 - > Multi
  //   1 1 0 - > Comp
  //   0 0 1 - > Shift
endmodule

module somador (
  input  A,
  input  B,
  input  CARRY,
  output s,
  output cout
);

  wire and_1_out, and_2_out, and_3_out, xor_1_out;

  xor xor_1 (xor_1_out, A, B);
  and and_1 (and_1_out, A, B);
  and and_2 (and_2_out, A, CARRY);
  and and_3 (and_3_out, B, CARRY);
  xor xor_2 (s, xor_1_out, CARRY);
  or or_1 (cout, and_1_out, and_2_out, and_3_out);
endmodule

module somador4bits (
  input  CARRY,
  input  B3,
  input  A3,
  input  B2,
  input  A2,
  input  B1,
  input  A1,
  input  B0,
  input  A0,
  output C3,
  output C2,
  output C1,
  output C0,
  output cout
);

  wire somador_2_cout, somador_3_cout, somador_4_cout;

  somador somador_1 (.A(A3), .B(B3), .CARRY(somador_2_cout), .s(C3), .cout(cout));
  somador somador_2 (.A(A2), .B(B2), .CARRY(somador_3_cout), .s(C2), .cout(somador_2_cout));
  somador somador_3 (.A(A1), .B(B1), .CARRY(somador_4_cout), .s(C1), .cout(somador_3_cout));
  somador somador_4 (.A(A0), .B(B0), .CARRY(CARRY), .s(C0), .cout(somador_4_cout));
endmodule

module somador8bits (
  input  B7,
  input  A7,
  input  B6,
  input  A6,
  input  B5,
  input  A5,
  input  B4,
  input  A4,
  input  B3,
  input  A3,
  input  B2,
  input  A2,
  input  B1,
  input  A1,
  input  B0,
  input  A0,
  output cout,
  output C7,
  output C6,
  output C5,
  output C4,
  output C3,
  output C2,
  output C1,
  output C0
);

  wire somador4bits_2_cout;

  somador4bits somador4bits_1 (
    .CARRY(somador4bits_2_cout), .B3(B7), .A3(A7), .B2(B6), .A2(A6), .B1(B5), .A1(A5), .B0(B4), .A0(A4),
    .C3(C7), .C2(C6), .C1(C5), .C0(C4), .cout(cout));
  somador4bits somador4bits_2 (
    .CARRY(1'b0), .B3(B3), .A3(A3), .B2(B2), .A2(A2), .B1(B1), .A1(A1), .B0(B0), .A0(A0), .C3(C3), .C2(C2),
    .C1(C1), .C0(C0), .cout(somador4bits_2_cout));
endmodule

module subtrator8bits (
  input  B7,
  input  B6,
  input  B5,
  input  B4,
  input  B3,
  input  B2,
  input  B1,
  input  B0,
  input  A7,
  input  A6,
  input  A5,
  input  A4,
  input  A3,
  input  A2,
  input  A1,
  input  A0,
  output cout,
  output C7,
  output C6,
  output C5,
  output C4,
  output C3,
  output C2,
  output C1,
  output C0
);

  wire not_1_out, not_2_out, not_3_out, not_4_out, not_5_out, not_6_out, not_7_out, not_8_out,
       somador8bits_1_c0, somador8bits_1_c1, somador8bits_1_c2, somador8bits_1_c3, somador8bits_1_c4,
       somador8bits_1_c5, somador8bits_1_c6, somador8bits_1_c7, somador8bits_1_cout;

  not not_1 (not_1_out, A7);
  not not_2 (not_2_out, A6);
  not not_3 (not_3_out, A5);
  not not_4 (not_4_out, A4);
  not not_5 (not_5_out, A3);
  not not_6 (not_6_out, A2);
  not not_7 (not_7_out, A1);
  not not_8 (not_8_out, A0);
  somador8bits somador8bits_1 (
    .B7(1'b0), .A7(not_1_out), .B6(1'b0), .A6(not_2_out), .B5(1'b0), .A5(not_3_out), .B4(1'b0),
    .A4(not_4_out), .B3(1'b0), .A3(not_5_out), .B2(1'b0), .A2(not_6_out), .B1(1'b0), .A1(not_7_out),
    .B0(1'b1), .A0(not_8_out), .cout(somador8bits_1_cout), .C7(somador8bits_1_c7), .C6(somador8bits_1_c6),
    .C5(somador8bits_1_c5), .C4(somador8bits_1_c4), .C3(somador8bits_1_c3), .C2(somador8bits_1_c2),
    .C1(somador8bits_1_c1), .C0(somador8bits_1_c0));
  somador8bits somador8bits_2 (
    .B7(B7), .A7(somador8bits_1_c7), .B6(B6), .A6(somador8bits_1_c6), .B5(B5), .A5(somador8bits_1_c5),
    .B4(B4), .A4(somador8bits_1_c4), .B3(B3), .A3(somador8bits_1_c3), .B2(B2), .A2(somador8bits_1_c2),
    .B1(B1), .A1(somador8bits_1_c1), .B0(B0), .A0(somador8bits_1_c0), .cout(cout), .C7(C7), .C6(C6), .C5(C5),
    .C4(C4), .C3(C3), .C2(C2), .C1(C1), .C0(C0));
  // also tied to GND on the sheet: somador8bits_1_cout
endmodule

module comparador8bits_test (
  input  B7,
  input  A7,
  input  B6,
  input  A6,
  output better,
  output lower,
  output equal
);

  wire and_1_out, and_2_out, and_3_out, and_4_out, and_5_out, and_6_out, and_7_out, and_8_out, and_9_out,
       and_10_out, or_1_out, or_2_out, xor_1_out, xor_2_out, xor_3_out, xor_4_out;

  xor xor_1 (xor_1_out, B7, A7);
  and and_1 (and_1_out, B7, A7);
  and and_2 (and_2_out, B6, A6);
  and and_3 (and_3_out, and_1_out, B6);
  and and_4 (and_4_out, and_1_out, A6);
  and and_5 (and_5_out, and_2_out, 1'b0);
  and and_6 (and_6_out, and_2_out, 1'b0);
  and and_7 (and_7_out, B7, xor_1_out);
  and and_8 (and_8_out, A7, xor_1_out);
  or or_1 (or_1_out, and_3_out, and_4_out);
  or or_2 (or_2_out, and_5_out, and_6_out);
  xor xor_2 (xor_2_out, and_1_out, or_1_out);
  xor xor_3 (xor_3_out, B6, A6);
  xor xor_4 (xor_4_out, and_2_out, or_2_out);
  and and_9 (and_9_out, B6, xor_3_out);
  and and_10 (and_10_out, xor_3_out, A6);
  or or_3 (better, and_7_out, and_9_out);
  or or_4 (lower, and_8_out, and_10_out);
  or or_5 (equal, xor_2_out, xor_4_out);
endmodule

module comparador1bit (
  input  B0,
  input  A0,
  input  r_BT,
  input  r_LW,
  input  r_EQ,
  output BT,
  output LW,
  output EQ
);

  wire and_1_out, and_2_out, and_3_out, and_4_out, and_5_out, and_6_out, and_7_out, not_1_out, not_2_out,
       not_3_out, not_4_out, not_5_out, not_6_out, xor_1_out;

  xor xor_1 (xor_1_out, B0, A0);
  and and_1 (and_1_out, B0, A0);
  and and_2 (and_2_out, B0, xor_1_out);
  and and_3 (and_3_out, A0, xor_1_out);
  not not_1 (not_1_out, r_LW);
  not not_2 (not_2_out, r_BT);
  and and_4 (and_4_out, and_2_out, not_1_out);
  and and_5 (and_5_out, and_3_out, not_2_out);
  or or_1 (BT, and_4_out, r_BT);
  or or_2 (LW, and_5_out, r_LW);
  not not_3 (not_3_out, r_BT);
  not not_4 (not_4_out, r_LW);
  and and_6 (and_6_out, and_1_out, not_3_out, not_4_out);
  not not_5 (not_5_out, B0);
  not not_6 (not_6_out, A0);
  and and_7 (and_7_out, not_5_out, not_6_out, r_EQ);
  or or_3 (EQ, and_6_out, and_7_out);
endmodule

module comparador8bits (
  input  B7,
  input  B6,
  input  B5,
  input  B4,
  input  B3,
  input  B2,
  input  B1,
  input  B0,
  input  A7,
  input  A6,
  input  A5,
  input  A4,
  input  A3,
  input  A2,
  input  A1,
  input  A0,
  output BT,
  output LW,
  output EQ
);

  wire comparador4bits_1_bt, comparador4bits_1_eq, comparador4bits_1_lw;

  comparador4bits comparador4bits_1 (
    .r_BT(1'b0), .r_LW(1'b0), .r_EQ(1'b0), .B3(B7), .A3(A7), .B2(B6), .A2(A6), .B1(B5), .A1(A5), .B0(B4),
    .A0(A4), .BT(comparador4bits_1_bt), .LW(comparador4bits_1_lw), .EQ(comparador4bits_1_eq));
  comparador4bits comparador4bits_2 (
    .r_BT(comparador4bits_1_bt), .r_LW(comparador4bits_1_lw), .r_EQ(comparador4bits_1_eq), .B3(B3), .A3(A3),
    .B2(B2), .A2(A2), .B1(B1), .A1(A1), .B0(B0), .A0(A0), .BT(BT), .LW(LW), .EQ(EQ));
endmodule

module comparadorbasico1bit (
  input  in_1,
  input  in_2,
  output better,
  output lower,
  output equal
);

  wire xor_1_out;

  xor xor_1 (xor_1_out, in_1, in_2);
  and and_1 (equal, in_1, in_2);
  and and_2 (better, in_1, xor_1_out);
  and and_3 (lower, in_2, xor_1_out);
endmodule

module comparador4bits (
  input  r_BT,
  input  r_LW,
  input  r_EQ,
  input  B3,
  input  A3,
  input  B2,
  input  A2,
  input  B1,
  input  A1,
  input  B0,
  input  A0,
  output BT,
  output LW,
  output EQ
);

  wire comparador1bit_1_bt, comparador1bit_1_eq, comparador1bit_1_lw, comparador1bit_2_bt,
       comparador1bit_2_eq, comparador1bit_2_lw, comparador1bit_3_bt, comparador1bit_3_eq,
       comparador1bit_3_lw;

  comparador1bit comparador1bit_1 (
    .B0(B3), .A0(A3), .r_BT(r_BT), .r_LW(r_LW), .r_EQ(r_EQ), .BT(comparador1bit_1_bt),
    .LW(comparador1bit_1_lw), .EQ(comparador1bit_1_eq));
  comparador1bit comparador1bit_2 (
    .B0(B2), .A0(A2), .r_BT(comparador1bit_1_bt), .r_LW(comparador1bit_1_lw), .r_EQ(comparador1bit_1_eq),
    .BT(comparador1bit_2_bt), .LW(comparador1bit_2_lw), .EQ(comparador1bit_2_eq));
  comparador1bit comparador1bit_3 (
    .B0(B1), .A0(A1), .r_BT(comparador1bit_2_bt), .r_LW(comparador1bit_2_lw), .r_EQ(comparador1bit_2_eq),
    .BT(comparador1bit_3_bt), .LW(comparador1bit_3_lw), .EQ(comparador1bit_3_eq));
  comparador1bit comparador1bit_4 (
    .B0(B0), .A0(A0), .r_BT(comparador1bit_3_bt), .r_LW(comparador1bit_3_lw), .r_EQ(comparador1bit_3_eq),
    .BT(BT), .LW(LW), .EQ(EQ));
endmodule

module multiplicador8bits (
  input  A3,
  input  A2,
  input  A1,
  input  A0,
  input  B3,
  input  B2,
  input  B1,
  input  B0,
  output S7,
  output S6,
  output S5,
  output S4,
  output S3,
  output S2,
  output S1,
  output S0
);

  wire and_1_out, and_2_out, and_3_out, and_4_out, and_5_out, and_6_out, and_7_out, and_8_out, and_9_out,
       and_10_out, and_11_out, and_12_out, and_13_out, and_14_out, and_15_out, somador4bits_2_c1,
       somador4bits_2_c2, somador4bits_2_c3, somador4bits_2_cout, somador4bits_3_c1, somador4bits_3_c2,
       somador4bits_3_c3, somador4bits_3_cout;

  and and_1 (and_1_out, B3, A3);
  and and_2 (and_2_out, B3, A2);
  and and_3 (and_3_out, B3, A1);
  and and_4 (and_4_out, B3, A0);
  and and_5 (and_5_out, B2, A3);
  and and_6 (and_6_out, B2, A2);
  and and_7 (and_7_out, B2, A1);
  and and_8 (and_8_out, B2, A0);
  somador4bits somador4bits_1 (
    .B3(somador4bits_2_cout), .A3(and_1_out), .B2(somador4bits_2_c3), .A2(and_2_out), .B1(somador4bits_2_c2),
    .A1(and_3_out), .B0(somador4bits_2_c1), .A0(and_4_out), .C3(S6), .C2(S5), .C1(S4), .C0(S3), .cout(S7));  // open: CARRY
  and and_9 (and_9_out, B1, A3);
  and and_10 (and_10_out, B1, A2);
  and and_11 (and_11_out, B1, A1);
  and and_12 (and_12_out, B1, A0);
  somador4bits somador4bits_2 (
    .B3(somador4bits_3_cout), .A3(and_5_out), .B2(somador4bits_3_c3), .A2(and_6_out), .B1(somador4bits_3_c2),
    .A1(and_7_out), .B0(somador4bits_3_c1), .A0(and_8_out), .C3(somador4bits_2_c3), .C2(somador4bits_2_c2),
    .C1(somador4bits_2_c1), .C0(S2), .cout(somador4bits_2_cout));  // open: CARRY
  and and_13 (and_13_out, B0, A3);
  and and_14 (and_14_out, B0, A2);
  and and_15 (and_15_out, B0, A1);
  somador4bits somador4bits_3 (
    .CARRY(1'b0), .B3(1'b0), .A3(and_9_out), .B2(and_13_out), .A2(and_10_out), .B1(and_14_out),
    .A1(and_11_out), .B0(and_15_out), .A0(and_12_out), .C3(somador4bits_3_c3), .C2(somador4bits_3_c2),
    .C1(somador4bits_3_c1), .C0(S1), .cout(somador4bits_3_cout));
  and and_16 (S0, B0, A0);
endmodule

module bitshift (
  input  A7,
  input  A6,
  input  A5,
  input  A4,
  input  A3,
  input  A2,
  input  A1,
  input  A0,
  output cout,
  output C7,
  output C6,
  output C5,
  output C4,
  output C3,
  output C2,
  output C1,
  output C0
);

  wire clock_1_out;

  Clock clock_1 (.out(clock_1_out));
  D_Flip_Flop d_ff_1 (.D(A7), .clk(clock_1_out), .Q(cout));  // open: Qn, preset, reset
  D_Flip_Flop d_ff_2 (.D(A6), .clk(clock_1_out), .Q(C7));  // open: Qn, preset, reset
  D_Flip_Flop d_ff_3 (.D(A5), .clk(clock_1_out), .Q(C6));  // open: Qn, preset, reset
  D_Flip_Flop d_ff_4 (.D(A4), .clk(clock_1_out), .Q(C5));  // open: Qn, preset, reset
  D_Flip_Flop d_ff_5 (.D(A3), .clk(clock_1_out), .Q(C4));  // open: Qn, preset, reset
  D_Flip_Flop d_ff_6 (.D(A2), .clk(clock_1_out), .Q(C3));  // open: Qn, preset, reset
  D_Flip_Flop d_ff_7 (.D(A1), .clk(clock_1_out), .Q(C2));  // open: Qn, preset, reset
  D_Flip_Flop d_ff_8 (.D(A0), .clk(clock_1_out), .Q(C1));  // open: Qn, preset, reset
  and and_1 (C0, A0, 1'b0);
endmodule

module ALU8bits (
  input  OP0,
  input  OP1,
  input  OP2,
  input  B7,
  input  A7,
  input  B6,
  input  A6,
  input  B5,
  input  A5,
  input  B4,
  input  A4,
  input  B3,
  input  A3,
  input  B2,
  input  A2,
  input  B1,
  input  A1,
  input  B0,
  input  A0,
  output cout,
  output C7,
  output C6,
  output C5,
  output C4,
  output C3,
  output C2,
  output C1,
  output C0,
  output EQ,
  output LW,
  output BT
);

  wire and_1_out, and_2_out, and_3_out, and_4_out, and_5_out, and_6_out, and_7_out, and_8_out, and_9_out,
       and_10_out, and_11_out, and_12_out, and_13_out, and_14_out, and_15_out, and_16_out, and_17_out,
       and_18_out, and_19_out, and_20_out, and_21_out, and_22_out, and_23_out, and_24_out, and_25_out,
       and_26_out, and_27_out, and_28_out, and_29_out, and_30_out, and_31_out, and_32_out, and_33_out,
       and_34_out, and_35_out, and_36_out, and_37_out, and_38_out, and_39_out, and_40_out, and_41_out,
       and_42_out, and_43_out, and_44_out, and_45_out, and_46_out, and_47_out, and_48_out, and_49_out,
       and_50_out, and_51_out, and_52_out, and_53_out, and_54_out, and_55_out, and_56_out, and_57_out,
       and_58_out, and_59_out, and_60_out, and_61_out, and_62_out, and_63_out, and_64_out, bitshift_1_c0,
       bitshift_1_c1, bitshift_1_c2, bitshift_1_c3, bitshift_1_c4, bitshift_1_c5, bitshift_1_c6,
       bitshift_1_c7, bitshift_1_cout, Comp_out, Multi_out, multiplicador8bits_1_s0, multiplicador8bits_1_s1,
       multiplicador8bits_1_s2, multiplicador8bits_1_s3, multiplicador8bits_1_s4, multiplicador8bits_1_s5,
       multiplicador8bits_1_s6, multiplicador8bits_1_s7, not_1_out, not_2_out, not_3_out, not_4_out,
       not_5_out, not_6_out, not_7_out, not_8_out, not_9_out, not_10_out, Shift_out, somador8bits_1_c0,
       somador8bits_1_c1, somador8bits_1_c2, somador8bits_1_c3, somador8bits_1_c4, somador8bits_1_c5,
       somador8bits_1_c6, somador8bits_1_c7, somador8bits_1_cout, Sub_out, subtrator8bits_1_c0,
       subtrator8bits_1_c1, subtrator8bits_1_c2, subtrator8bits_1_c3, subtrator8bits_1_c4,
       subtrator8bits_1_c5, subtrator8bits_1_c6, subtrator8bits_1_c7, subtrator8bits_1_cout, Sum_out;

  not not_1 (not_1_out, OP2);
  not not_2 (not_2_out, OP0);
  not not_3 (not_3_out, OP1);
  not not_4 (not_4_out, OP0);
  not not_5 (not_5_out, OP2);
  and Comp (Comp_out, OP0, OP1, not_1_out);
  and Shift (Shift_out, not_2_out, not_3_out, OP2);
  not not_6 (not_6_out, OP0);
  not not_7 (not_7_out, OP1);
  not not_8 (not_8_out, OP2);
  not not_9 (not_9_out, OP1);
  not not_10 (not_10_out, OP2);
  and Multi (Multi_out, not_4_out, OP1, not_5_out);
  and Sum (Sum_out, not_6_out, not_7_out, not_8_out);
  and Sub (Sub_out, OP0, not_9_out, not_10_out);
  and and_1 (and_1_out, B7, Sub_out);
  and and_2 (and_2_out, B6, Sub_out);
  and and_3 (and_3_out, B5, Sub_out);
  and and_4 (and_4_out, B4, Sub_out);
  and and_5 (and_5_out, B3, Sub_out);
  and and_6 (and_6_out, B2, Sub_out);
  and and_7 (and_7_out, B1, Sub_out);
  and and_8 (and_8_out, B0, Sub_out);
  and and_9 (and_9_out, A7, Sub_out);
  and and_10 (and_10_out, A6, Sub_out);
  and and_11 (and_11_out, A5, Sub_out);
  and and_12 (and_12_out, A4, Sub_out);
  and and_13 (and_13_out, A3, Sub_out);
  and and_14 (and_14_out, A2, Sub_out);
  and and_15 (and_15_out, A1, Sub_out);
  and and_16 (and_16_out, A0, Sub_out);
  and and_17 (and_17_out, A3, Multi_out);
  and and_18 (and_18_out, A2, Multi_out);
  and and_19 (and_19_out, A1, Multi_out);
  and and_20 (and_20_out, A0, Multi_out);
  and and_21 (and_21_out, B3, Multi_out);
  and and_22 (and_22_out, B2, Multi_out);
  and and_23 (and_23_out, B1, Multi_out);
  and and_24 (and_24_out, B0, Multi_out);
  and and_25 (and_25_out, B7, Comp_out);
  and and_26 (and_26_out, B6, Comp_out);
  and and_27 (and_27_out, B5, Comp_out);
  and and_28 (and_28_out, B4, Comp_out);
  and and_29 (and_29_out, B3, Comp_out);
  and and_30 (and_30_out, B2, Comp_out);
  and and_31 (and_31_out, B1, Comp_out);
  and and_32 (and_32_out, B0, Comp_out);
  and and_33 (and_33_out, A7, Comp_out);
  and and_34 (and_34_out, A6, Comp_out);
  and and_35 (and_35_out, A5, Comp_out);
  and and_36 (and_36_out, A4, Comp_out);
  and and_37 (and_37_out, A3, Comp_out);
  and and_38 (and_38_out, A2, Comp_out);
  and and_39 (and_39_out, A1, Comp_out);
  and and_40 (and_40_out, A0, Comp_out);
  and and_41 (and_41_out, A7, Shift_out);
  and and_42 (and_42_out, A6, Shift_out);
  and and_43 (and_43_out, A5, Shift_out);
  and and_44 (and_44_out, A4, Shift_out);
  and and_45 (and_45_out, A3, Shift_out);
  and and_46 (and_46_out, A2, Shift_out);
  and and_47 (and_47_out, A1, Shift_out);
  and and_48 (and_48_out, A0, Shift_out);
  and and_49 (and_49_out, B7, Sum_out);
  and and_50 (and_50_out, A7, Sum_out);
  and and_51 (and_51_out, B6, Sum_out);
  and and_52 (and_52_out, A6, Sum_out);
  and and_53 (and_53_out, B5, Sum_out);
  and and_54 (and_54_out, A5, Sum_out);
  and and_55 (and_55_out, B4, Sum_out);
  and and_56 (and_56_out, A4, Sum_out);
  and and_57 (and_57_out, B3, Sum_out);
  and and_58 (and_58_out, A3, Sum_out);
  and and_59 (and_59_out, B2, Sum_out);
  and and_60 (and_60_out, A2, Sum_out);
  and and_61 (and_61_out, B1, Sum_out);
  and and_62 (and_62_out, A1, Sum_out);
  and and_63 (and_63_out, B0, Sum_out);
  and and_64 (and_64_out, A0, Sum_out);
  subtrator8bits subtrator8bits_1 (
    .B7(and_1_out), .B6(and_2_out), .B5(and_3_out), .B4(and_4_out), .B3(and_5_out), .B2(and_6_out),
    .B1(and_7_out), .B0(and_8_out), .A7(and_9_out), .A6(and_10_out), .A5(and_11_out), .A4(and_12_out),
    .A3(and_13_out), .A2(and_14_out), .A1(and_15_out), .A0(and_16_out), .cout(subtrator8bits_1_cout),
    .C7(subtrator8bits_1_c7), .C6(subtrator8bits_1_c6), .C5(subtrator8bits_1_c5), .C4(subtrator8bits_1_c4),
    .C3(subtrator8bits_1_c3), .C2(subtrator8bits_1_c2), .C1(subtrator8bits_1_c1), .C0(subtrator8bits_1_c0));
  multiplicador8bits multiplicador8bits_1 (
    .A3(and_17_out), .A2(and_18_out), .A1(and_19_out), .A0(and_20_out), .B3(and_21_out), .B2(and_22_out),
    .B1(and_23_out), .B0(and_24_out), .S7(multiplicador8bits_1_s7), .S6(multiplicador8bits_1_s6),
    .S5(multiplicador8bits_1_s5), .S4(multiplicador8bits_1_s4), .S3(multiplicador8bits_1_s3),
    .S2(multiplicador8bits_1_s2), .S1(multiplicador8bits_1_s1), .S0(multiplicador8bits_1_s0));
  comparador8bits comparador8bits_1 (
    .B7(and_25_out), .B6(and_26_out), .B5(and_27_out), .B4(and_28_out), .B3(and_29_out), .B2(and_30_out),
    .B1(and_31_out), .B0(and_32_out), .A7(and_33_out), .A6(and_34_out), .A5(and_35_out), .A4(and_36_out),
    .A3(and_37_out), .A2(and_38_out), .A1(and_39_out), .A0(and_40_out), .BT(BT), .LW(LW), .EQ(EQ));
  bitshift bitshift_1 (
    .A7(and_41_out), .A6(and_42_out), .A5(and_43_out), .A4(and_44_out), .A3(and_45_out), .A2(and_46_out),
    .A1(and_47_out), .A0(and_48_out), .cout(bitshift_1_cout), .C7(bitshift_1_c7), .C6(bitshift_1_c6),
    .C5(bitshift_1_c5), .C4(bitshift_1_c4), .C3(bitshift_1_c3), .C2(bitshift_1_c2), .C1(bitshift_1_c1),
    .C0(bitshift_1_c0));
  somador8bits somador8bits_1 (
    .B7(and_49_out), .A7(and_50_out), .B6(and_51_out), .A6(and_52_out), .B5(and_53_out), .A5(and_54_out),
    .B4(and_55_out), .A4(and_56_out), .B3(and_57_out), .A3(and_58_out), .B2(and_59_out), .A2(and_60_out),
    .B1(and_61_out), .A1(and_62_out), .B0(and_63_out), .A0(and_64_out), .cout(somador8bits_1_cout),
    .C7(somador8bits_1_c7), .C6(somador8bits_1_c6), .C5(somador8bits_1_c5), .C4(somador8bits_1_c4),
    .C3(somador8bits_1_c3), .C2(somador8bits_1_c2), .C1(somador8bits_1_c1), .C0(somador8bits_1_c0));
  or or_1 (cout, subtrator8bits_1_cout, bitshift_1_cout, somador8bits_1_cout);
  or or_2 (C7, subtrator8bits_1_c7, multiplicador8bits_1_s7, bitshift_1_c7, somador8bits_1_c7);
  or or_3 (C6, subtrator8bits_1_c6, multiplicador8bits_1_s6, bitshift_1_c6, somador8bits_1_c6);
  or or_4 (C5, subtrator8bits_1_c5, multiplicador8bits_1_s5, bitshift_1_c5, somador8bits_1_c5);
  or or_5 (C4, subtrator8bits_1_c4, multiplicador8bits_1_s4, bitshift_1_c4, somador8bits_1_c4);
  or or_6 (C3, subtrator8bits_1_c3, multiplicador8bits_1_s3, bitshift_1_c3, somador8bits_1_c3);
  or or_7 (C2, subtrator8bits_1_c2, multiplicador8bits_1_s2, bitshift_1_c2, somador8bits_1_c2);
  or or_8 (C1, subtrator8bits_1_c1, multiplicador8bits_1_s1, bitshift_1_c1, somador8bits_1_c1);
  or or_9 (C0, subtrator8bits_1_c0, multiplicador8bits_1_s0, bitshift_1_c0, somador8bits_1_c0);
endmodule

module bcd (
  input  A,
  input  B,
  input  C,
  input  D,
  output s_a,
  output s_b,
  output s_c,
  output s_d,
  output s_e,
  output s_f,
  output s_g
);

  wire and_1_out, and_2_out, and_3_out, and_4_out, and_5_out, and_6_out, and_7_out, and_8_out, and_9_out,
       and_10_out, and_11_out, and_12_out, and_13_out, and_14_out, and_15_out, and_16_out, not_1_out,
       not_2_out, not_3_out;

  not not_1 (not_1_out, B);
  not not_2 (not_2_out, C);
  not not_3 (not_3_out, D);
  and and_1 (and_1_out, not_1_out, not_3_out);
  and and_2 (and_2_out, B, D);
  and and_3 (and_3_out, not_2_out, not_3_out);
  and and_4 (and_4_out, C, D);
  or or_1 (s_c, not_2_out, D, B);
  and and_5 (and_5_out, not_1_out, not_3_out);
  and and_6 (and_6_out, not_1_out, C);
  and and_7 (and_7_out, B, not_2_out, D);
  and and_8 (and_8_out, C, not_3_out);
  and and_9 (and_9_out, not_1_out, not_3_out);
  and and_10 (and_10_out, C, not_3_out);
  and and_11 (and_11_out, not_2_out, not_3_out);
  and and_12 (and_12_out, B, not_2_out);
  and and_13 (and_13_out, B, not_3_out);
  and and_14 (and_14_out, not_1_out, C);
  and and_15 (and_15_out, B, not_2_out);
  and and_16 (and_16_out, C, not_3_out);
  or or_2 (s_a, and_1_out, C, and_2_out, A);
  or or_3 (s_b, not_1_out, and_3_out, and_4_out);
  or or_4 (s_d, and_5_out, and_6_out, and_7_out, and_8_out, A);
  or or_5 (s_e, and_9_out, and_10_out);
  or or_6 (s_f, and_11_out, and_12_out, and_13_out, A);
  or or_7 (s_g, and_14_out, and_15_out, A, and_16_out);
endmodule

module decimal_to_hexa (
  input  A,
  input  B,
  input  C,
  input  D,
  output s_a,
  output s_b,
  output s_c,
  output s_d,
  output s_e,
  output s_f,
  output s_g
);

  wire and_1_out, and_2_out, and_3_out, and_4_out, and_5_out, and_6_out, and_7_out, and_8_out, and_9_out,
       and_10_out, and_11_out, and_12_out, and_13_out, and_14_out, and_15_out, and_16_out, and_17_out,
       and_18_out, and_19_out, and_20_out, and_21_out, and_22_out, and_23_out, and_24_out, and_25_out,
       and_26_out, and_27_out, and_28_out, and_29_out, and_30_out, and_31_out, and_32_out, and_33_out,
       and_34_out, and_35_out, not_1_out, not_2_out, not_3_out, not_4_out;

  not not_1 (not_1_out, A);
  not not_2 (not_2_out, B);
  not not_3 (not_3_out, C);
  not not_4 (not_4_out, D);
  and and_1 (and_1_out, not_2_out, not_4_out);
  and and_2 (and_2_out, not_1_out, C);
  and and_3 (and_3_out, not_1_out, B, D);
  and and_4 (and_4_out, A, not_2_out, not_3_out);
  and and_5 (and_5_out, A, not_4_out);
  and and_6 (and_6_out, B, C);
  and and_7 (and_7_out, not_1_out, not_3_out, not_4_out);
  and and_8 (and_8_out, not_1_out, C, D);
  and and_9 (and_9_out, not_2_out, not_4_out);
  and and_10 (and_10_out, A, not_3_out, D);
  and and_11 (and_11_out, not_1_out, not_2_out);
  and and_12 (and_12_out, not_1_out, B);
  and and_13 (and_13_out, A, not_2_out);
  and and_14 (and_14_out, not_3_out, D);
  and and_15 (and_15_out, not_2_out, not_3_out);
  and and_16 (and_16_out, not_2_out, D);
  and and_17 (and_17_out, B, not_3_out, D);
  and and_18 (and_18_out, not_1_out, not_2_out, not_4_out);
  and and_19 (and_19_out, not_2_out, C, D);
  and and_20 (and_20_out, A, not_3_out);
  and and_21 (and_21_out, B, C, not_4_out);
  and and_22 (and_22_out, not_2_out, not_4_out);
  and and_23 (and_23_out, C, not_4_out);
  and and_24 (and_24_out, A, C);
  and and_25 (and_25_out, A, B);
  and and_26 (and_26_out, not_3_out, not_4_out);
  and and_27 (and_27_out, not_1_out, B, not_3_out);
  and and_28 (and_28_out, B, not_4_out);
  and and_29 (and_29_out, A, not_2_out);
  and and_30 (and_30_out, A, C);
  and and_31 (and_31_out, not_2_out, C);
  and and_32 (and_32_out, A, not_2_out);
  and and_33 (and_33_out, not_1_out, B, not_3_out);
  and and_34 (and_34_out, C, not_4_out);
  and and_35 (and_35_out, A, D);
  or or_1 (s_a, and_1_out, and_2_out, and_3_out, and_4_out, and_5_out, and_6_out);
  or or_2 (s_b, and_7_out, and_8_out, and_9_out, and_10_out, and_11_out);
  or or_3 (s_c, and_12_out, and_13_out, and_14_out, and_15_out, and_16_out);
  or or_4 (s_d, and_17_out, and_18_out, and_19_out, and_20_out, and_21_out);
  or or_5 (s_e, and_22_out, and_23_out, and_24_out, and_25_out);
  or or_6 (s_f, and_26_out, and_27_out, and_28_out, and_29_out, and_30_out);
  or or_7 (s_g, and_31_out, and_32_out, and_33_out, and_34_out, and_35_out);
endmodule

module registrador4bits (
  input  A3,
  input  A2,
  input  A1,
  input  A0,
  output Q3,
  output Q2,
  output Q1,
  output Q0
);

  wire clock_1_out;

  Clock clock_1 (.out(clock_1_out));
  D_Flip_Flop d_ff_1 (.D(A0), .clk(clock_1_out), .Q(Q0));  // open: Qn, preset, reset
  D_Flip_Flop d_ff_2 (.D(A1), .clk(clock_1_out), .Q(Q1));  // open: Qn, preset, reset
  D_Flip_Flop d_ff_3 (.D(A2), .clk(clock_1_out), .Q(Q2));  // open: Qn, preset, reset
  D_Flip_Flop d_ff_4 (.D(A3), .clk(clock_1_out), .Q(Q3));  // open: Qn, preset, reset
endmodule
